// Logisim project assignment-1-sim-2(1).circ as structural Verilog: 3 circuits, main circuit Mux Selection
module Mux_Selection (
  input  A,
  input  B,
  input  [2:0] s2_s1_s0,
  output out_4,
  output out_5
);

  wire and_1_out, and_3_out, not_1_out, not_2_out, or_1_out, xor_1_out;
  wire [1:0] or_2_out;

  xor xor_1 (xor_1_out, A, B);
  not not_1 (not_1_out, A);
  and and_1 (and_1_out, A, B);
  Multiplexer #(.select(2), .enable("false")) multiplexer_1 (
    .in0(xor_1_out), .in1(A), .in2(not_1_out), .in3(and_1_out), .out(out_4), .sel(or_2_out));
  Multiplexer #(.enable("false")) multiplexer_2 (.in0(1'b0), .in1(B), .out(out_5), .sel(and_3_out));
  and and_2 (or_2_out[1], or_1_out, s2_s1_s0[1]);
  or or_1 (or_1_out, s2_s1_s0[2], s2_s1_s0[0]);
  or or_2 (or_2_out[0], and_3_out, s2_s1_s0[2]);
  and and_3 (and_3_out, s2_s1_s0[0], not_2_out);
  not not_2 (not_2_out, s2_s1_s0[1]);
endmodule

module Alternate_ALU (
  input  [3:0] in_1,
  input  [3:0] in_2,
  input  [2:0] in_3,
  output out_4,
  output out_5,
  output [3:0] out_6,
  output out_7,
  output out_8
);

  wire adder_1_cout, and_1_out, xor_1_out;
  wire [3:0] Mux_selection_out_4, Mux_selection_out_5;

  Mux_Selection Mux_selection (
    .A(in_1[0]), .B(in_2[0]), .s2_s1_s0(in_3), .out_4(Mux_selection_out_4[0]), .out_5(Mux_selection_out_5[0]));
  Mux_Selection Mux_selection_2 (
    .A(in_1[1]), .B(in_2[1]), .s2_s1_s0(in_3), .out_4(Mux_selection_out_4[1]), .out_5(Mux_selection_out_5[1]));
  Mux_Selection Mux_selection_3 (
    .A(in_1[2]), .B(in_2[2]), .s2_s1_s0(in_3), .out_4(Mux_selection_out_4[2]), .out_5(Mux_selection_out_5[2]));
  Mux_Selection Mux_selection_4 (
    .A(in_1[3]), .B(in_2[3]), .s2_s1_s0(in_3), .out_4(Mux_selection_out_4[3]), .out_5(Mux_selection_out_5[3]));
  and and_1 (and_1_out, in_3[0], xor_1_out);
  xor xor_1 (xor_1_out, in_3[2], in_3[1]);
  Adder #(.width(4)) adder_1 (
    .a(Mux_selection_out_4), .b(Mux_selection_out_5), .out(out_6), .cin(and_1_out), .cout(adder_1_cout));
  Alternate_flag Flag_unit (
    .Cout(adder_1_cout), .Sum_bits(out_6), .X3__8(Mux_selection_out_4[3]), .Y3__11(Mux_selection_out_5[3]),
    .C(out_4), .Z(out_5), .S(out_7), .out_8(out_8));
endmodule

module Alternate_flag (
  input  Cout,
  input  [3:0] Sum_bits,
  input  X3__8,
  input  Y3__11,
  output C,
  output Z,
  output S,
  output out_8
);

  wire or_1_out, or_2_out, or_3_out, xor_1_out, xor_3_out;

  or or_1 (or_1_out, or_2_out, Sum_bits[3]);
  or or_2 (or_2_out, or_3_out, Sum_bits[2]);
  or or_3 (or_3_out, Sum_bits[0], Sum_bits[1]);
  xor xor_1 (xor_1_out, Y3__11, X3__8);
  xor xor_2 (out_8, xor_1_out, xor_3_out);
  xor xor_3 (xor_3_out, Sum_bits[3], Cout);
  not not_1 (Z, or_1_out);

  assign C = Cout;
  assign S = Sum_bits[3];
endmodule
