// Logisim project final.circ as structural Verilog: 2 circuits, main circuit main
module main (
  input  [31:0] B,
  input  [31:0] A,
  output [9:0] result_exp,
  output result_sign,
  output [21:0] result_frac
);

  wire comparator_1_gt, comparator_2_gt, multiplexer_1_out, multiplexer_2_out;
  wire [4:0] bit_extender_2_out, bit_extender_3_out, bitfinder_1_index, subtractor_2_out, subtractor_3_out;
  wire [9:0] multiplexer_6_out, multiplexer_8_out, subtractor_1_out;
  wire [21:0] bit_extender_1_out, bit_extender_4_out, bit_extender_6_out, multiplexer_7_out,
       multiplexer_9_out, shifter_1_out;
  wire [31:0] adder_1_out, bit_extender_5_out, bit_extender_7_out, multiplexer_3_out, multiplexer_4_out,
       multiplexer_10_out, negator_1_out, negator_2_out, negator_3_out, shifter_2_out;

  Multiplexer multiplexer_1 (.in0(B[31]), .in1(A[31]), .out(multiplexer_1_out), .sel(comparator_1_gt));  // open: en
  Negator #(.width(32)) negator_1 (.in(bit_extender_7_out), .out(negator_1_out));
  Negator #(.width(32)) negator_2 (.in(bit_extender_5_out), .out(negator_2_out));
  Multiplexer multiplexer_2 (.in0(A[31]), .in1(B[31]), .out(multiplexer_2_out), .sel(comparator_1_gt));  // open: en
  Multiplexer #(.width(32)) multiplexer_3 (
    .in0(bit_extender_7_out), .in1(negator_1_out), .out(multiplexer_3_out), .sel(multiplexer_1_out));  // open: en
  // Probe on multiplexer_3_out
  Multiplexer #(.width(32)) multiplexer_4 (
    .in0(bit_extender_5_out), .in1(negator_2_out), .out(multiplexer_4_out), .sel(multiplexer_2_out));  // open: en
  Comparator #(.width(10)) comparator_1 (.a(A[30:21]), .b(B[30:21]), .gt(comparator_1_gt));  // open: eq, lt
  Multiplexer #(.width(10)) multiplexer_5 (
    .in0(B[30:21]), .in1(A[30:21]), .out(result_exp), .sel(comparator_1_gt));  // open: en
  // Probe on bit_extender_1_out
  assign bit_extender_1_out = {{1{1'b1}}, A[20:0]};  // Bit_Extender bit_extender_1
  Multiplexer #(.width(10)) multiplexer_6 (
    .in0(A[30:21]), .in1(B[30:21]), .out(multiplexer_6_out), .sel(comparator_1_gt));  // open: en
  // Probe on subtractor_1_out
  Subtractor #(.width(10)) subtractor_1 (
    .a(result_exp), .b(multiplexer_6_out), .out(subtractor_1_out));  // open: bin, bout
  // Probe on 10'h16
  Bit_Extender #(.in_width(10), .out_width(5)) bit_extender_2 (.in(10'h16), .out(bit_extender_2_out));
  Comparator #(.width(10)) comparator_2 (.a(subtractor_1_out), .b(10'h16), .gt(comparator_2_gt));  // open: eq, lt
  Subtractor #(.width(5)) subtractor_2 (
    .a(bit_extender_2_out), .b(5'b00001), .out(subtractor_2_out));  // open: bin, bout
  Multiplexer #(.width(22)) multiplexer_7 (
    .in0(bit_extender_4_out), .in1(bit_extender_1_out), .out(multiplexer_7_out), .sel(comparator_1_gt));  // open: en
  Multiplexer #(.width(10)) multiplexer_8 (
    .in0(subtractor_1_out), .in1(10'h16), .out(multiplexer_8_out), .sel(comparator_2_gt));  // open: en
  // Probe on subtractor_2_out
  Multiplexer #(.width(22)) multiplexer_9 (
    .in0(bit_extender_1_out), .in1(bit_extender_4_out), .out(multiplexer_9_out), .sel(comparator_1_gt));  // open: en
  Bit_Extender #(.in_width(10), .out_width(5)) bit_extender_3 (.in(multiplexer_8_out), .out(bit_extender_3_out));
  // Probe on bit_extender_3_out
  Negator #(.width(32)) negator_3 (.in(adder_1_out), .out(negator_3_out));
  BitFinder #(.width(22), .\type ("high1")) bitfinder_1 (
    .in(bit_extender_6_out), .index(bitfinder_1_index));  // open: found
  // Probe on bitfinder_1_index
  assign bit_extender_4_out = {{1{1'b1}}, B[20:0]};  // Bit_Extender bit_extender_4
  // Probe on bit_extender_4_out
  Shifter #(.width(22), .shift("lr")) shifter_1 (
    .in(multiplexer_9_out), .\dist (bit_extender_3_out), .out(shifter_1_out));
  Adder #(.width(32)) adder_1 (.a(multiplexer_3_out), .b(multiplexer_4_out), .out(adder_1_out));  // open: cin, cout
  Multiplexer #(.width(32)) multiplexer_10 (
    .in0(adder_1_out), .in1(negator_3_out), .out(multiplexer_10_out), .sel(result_sign));  // open: en
  // Probe on multiplexer_10_out
  Subtractor #(.width(5)) subtractor_3 (
    .a(subtractor_2_out), .b(bitfinder_1_index), .out(subtractor_3_out));  // open: bin, bout
  // Probe on shifter_1_out
  assign bit_extender_5_out = {{10{1'b0}}, shifter_1_out};  // Bit_Extender bit_extender_5
  // Probe on adder_1_out
  Bit_Extender #(.in_width(32), .out_width(22)) bit_extender_6 (.in(multiplexer_10_out), .out(bit_extender_6_out));
  // Probe on subtractor_3_out
  // Probe on multiplexer_7_out
  // Probe on bit_extender_5_out
  Shifter #(.width(32), .shift("lr")) shifter_2 (.in(adder_1_out), .\dist ({5{1'b1}}), .out(shifter_2_out));
  // Probe on shifter_2_out
  // Probe on bit_extender_6_out
  Shifter #(.width(22)) shifter_3 (.in(bit_extender_6_out), .\dist (subtractor_3_out), .out(result_frac));
  // Probe on bit_extender_7_out
  assign bit_extender_7_out = {{10{1'b0}}, multiplexer_7_out};  // Bit_Extender bit_extender_7
  Bit_Extender #(.in_width(32), .out_width(1)) bit_extender_8 (.in(shifter_2_out), .out(result_sign));

  // Notes on the sheet:
  //   L sign
  //   -L
  //   -S
  //   signed L
  //   S sign
  //   A exp
  //   signed S
  //   A frac
  //   L(exp)
  //   A (with normalized 1)
  //   S(exp)
  //   B exp
  //   L-S
  //   A > B => A(larger)
  //   B frac
  //   A <= B => A(smaller)
  //   B (with normalized 1)
  //   S frac
  //   L frac
endmodule

module test (
  input  [2:0] GRS_BIT,
  input  [28:0] Add_Frac
);

  // Probe on {Add_Frac, GRS_BIT}
endmodule
